// Logisim project CPU.circ as structural Verilog: 1 circuit, main circuit main
// CPU
module main (
  input  [31:0] INSTRUCTION,
  input  [23:0] CURRENT_PC,
  input  CQ_PASSED,
  input  [31:0] REG_1_VAL,
  input  [31:0] REG_2_VAL,
  input  [31:0] REG_3_VAL,
  input  [31:0] ALU_RESULT,
  input  [31:0] MEM_OUT,
  output [23:0] JUMP_ADDRESS,
  output [2:0] CQ_QUERY,
  output CR_WRITE,
  output [3:0] REG_1_READ,
  output [3:0] REG_2_READ,
  output [3:0] REG_3_WRITE,
  output [31:0] REG_WRITE_VAL,
  output REG_WRITE,
  output [31:0] ALU_SOURCE_X,
  output [31:0] ALU_SOURCE_Y,
  output [3:0] ALU_OPERATION,
  output [23:0] MEM_ADDR,
  output [31:0] MEM_IN,
  output MEM_WRITE
);

  wire clk, comparator_1_eq, comparator_2_eq, comparator_3_eq, comparator_4_eq, comparator_6_eq,
       comparator_7_lt, CQ_Cmd, CQ_Output, Jump_Cmd, Link_Cmd, Load_Cmd, memWrite, not_1_out, not_2_out,
       not_3_out, not_4_out, or_1_out, prev_jump, write;
  wire [1:0] A_Type;
  wire [31:0] multiplexer_1_out, shifter_1_out;

  Shifter #(.width(32), .shift("lr")) shifter_1 (.in(INSTRUCTION), .\dist (5'b11100), .out(shifter_1_out));
  Bit_Extender #(.in_width(32), .out_width(4)) bit_extender_1 (.in(shifter_1_out), .out(ALU_OPERATION));
  Multiplexer #(.select(2), .width(32), .enable("false")) multiplexer_1 (
    .in0(REG_1_VAL), .in1(REG_2_VAL), .in3(REG_3_VAL), .out(multiplexer_1_out));  // open: in2, sel
  not not_1 (not_1_out, ALU_OPERATION[0]);
  not not_2 (not_2_out, ALU_OPERATION[1]);
  not not_3 (not_3_out, ALU_OPERATION[2]);
  not not_4 (not_4_out, ALU_OPERATION[3]);
  and and_1 (MEM_WRITE, ALU_OPERATION[0], not_2_out, ALU_OPERATION[2], ALU_OPERATION[3]);
  Comparator #(.width(4), .mode("unsigned")) comparator_1 (
    .a(ALU_OPERATION), .b(4'b1011), .eq(comparator_1_eq));  // open: gt, lt
  // AND_Gate and_2 is placed but not wired
  Comparator #(.width(4), .mode("unsigned")) comparator_2 (
    .a(ALU_OPERATION), .b(4'b1111), .eq(comparator_2_eq));  // open: gt, lt
  and and_3 (Jump_Cmd, comparator_2_eq, prev_jump, CQ_Output);
  Comparator #(.width(4), .mode("unsigned")) comparator_3 (
    .a(ALU_OPERATION), .b(4'b1010), .eq(comparator_3_eq));  // open: gt, lt
  and and_4 (Load_Cmd, comparator_3_eq, prev_jump, CQ_Output);
  and and_5 (memWrite, comparator_1_eq, prev_jump, CQ_Output);
  Comparator #(.width(32)) comparator_4 (.a(32'hf), .eq(comparator_4_eq));  // open: b, gt, lt
  Comparator #(.width(4), .mode("unsigned")) comparator_5 (
    .a(ALU_OPERATION), .b(4'b1110), .eq(Link_Cmd));  // open: gt, lt
  Comparator #(.width(2)) comparator_6 (.a(2'b01), .b(A_Type), .eq(comparator_6_eq));  // open: gt, lt
  Comparator #(.width(4), .mode("unsigned")) comparator_7 (
    .a(ALU_OPERATION), .b(4'b1011), .lt(comparator_7_lt));  // open: gt, eq
  and and_6 (CQ_Cmd, comparator_6_eq, prev_jump, CQ_Output);
  or or_1 (or_1_out, comparator_7_lt, Link_Cmd);
  and and_7 (write, CQ_Output, prev_jump, clk, or_1_out);

  // Other names for the same wires on the sheet: MEM_ID[31:0] = MEM_IN; memStore = MEM_WRITE; Save_Cmd = memWrite;
  //   OP_Code[3:0] = ALU_OPERATION

  // Notes on the sheet:
  //   INSTRUCTION MODULE
  //   CR MODULE
  //   REGISTER FILE MODULE
  //   ALU MODULE
  //   MEMORY MODULE
  //   Control
  //   Is this  set CQ command?
  //   Can REG write?
endmodule
